// Logisim project ALU.circ as structural Verilog: 9 circuits, main circuit  Main ALU Circuit
module _16_Bit_AND (
  input  [15:0] Input_A,
  input  [15:0] Input_B,
  output [15:0] Output
);

  assign Output = Input_A & Input_B;  // AND_Gate AND, 16 bits wide

  // Notes on the sheet:
  //   16-Bit AND
endmodule

module _16_Bit_OR (
  input  [15:0] Input_A,
  input  [15:0] Input_B,
  output [15:0] Ouput
);

  assign Ouput = Input_A | Input_B;  // OR_Gate OR, 16 bits wide

  // Notes on the sheet:
  //   16-Bit OR
endmodule

module _16_Bit_XOR (
  input  [15:0] Input_A,
  input  [15:0] Input_B,
  output [15:0] Ouput
);

  assign Ouput = Input_A ^ Input_B;  // XOR_Gate XOR, 16 bits wide

  // Notes on the sheet:
  //   16-bit XOR
endmodule

module _16_Bit_Inverter (
  input  [15:0] Input_A,
  output [15:0] Output
);

  assign Output = ~Input_A;  // NOT_Gate NOT, 16 bits wide

  // Notes on the sheet:
  //   16-Bit Inverter
endmodule

module _16_Bit_Adder (
  input  Carry_in,
  input  [15:0] Input_A,
  input  [15:0] Input_B,
  input  [15:0] in_4,
  output Negative,
  output [15:0] Ouput,
  output Zero,
  output Carry,
  output Overflow
);

  wire AND_2_out, AND_out, not_1_out, not_2_out, not_3_out, XOR_out;

  Adder #(.width(16)) adder_1 (.a(Input_A), .b(Input_B), .out({Negative, Ouput[14:0]}), .cin(Carry_in), .cout(Carry));
  xor XOR (XOR_out, Input_B[15], Carry_in);
  not not_1 (not_1_out, Negative);
  Comparator #(.width(16)) comparator_1 (.a({Negative, Ouput[14:0]}), .b(in_4), .eq(Zero));  // open: gt, lt
  not not_2 (not_2_out, XOR_out);
  not not_3 (not_3_out, Input_A[15]);
  and AND (AND_out, XOR_out, not_1_out, Input_A[15]);
  and AND_2 (AND_2_out, not_2_out, not_3_out, Negative);
  or OR (Overflow, AND_out, AND_2_out);

  assign Ouput[15] = Negative;

  // Notes on the sheet:
  //   16-Bit Adder
  //   Please notice that you need to generate the four flag bits for the adder.
endmodule

module _16_Bit_Subtractor (
  input  Carry_IN,
  input  [15:0] Input_A,
  input  [15:0] Input_B,
  input  [15:0] in_4,
  output Negative,
  output [15:0] Output,
  output Zero,
  output Carry,
  output Overflow
);

  wire AND_2_out, AND_out, not_1_out, not_2_out, not_3_out, XOR_out;

  Subtractor #(.width(16)) subtractor_1 (
    .a(Input_A), .b(Input_B), .out({Negative, Output[14:0]}), .bin(Carry_IN), .bout(Carry));
  xor XOR (XOR_out, Input_B[15], Carry_IN);
  not not_1 (not_1_out, Negative);
  Comparator #(.width(16)) comparator_1 (.a({Negative, Output[14:0]}), .b(in_4), .eq(Zero));  // open: gt, lt
  not not_2 (not_2_out, XOR_out);
  not not_3 (not_3_out, Input_A[15]);
  and AND (AND_out, XOR_out, not_1_out, Input_A[15]);
  and AND_2 (AND_2_out, not_2_out, not_3_out, Negative);
  or OR (Overflow, AND_out, AND_2_out);

  assign Output[15] = Negative;

  // Notes on the sheet:
  //   16-Bit Subtractor
  //   Please notice that you need to generate the four flag bits for the subtractor
endmodule

module _16_Bit_Left_Shifter_Circuit (
  input  [15:0] Input_A,
  input  [3:0] Input_B,
  input  Enable,
  input  _1_Input_Bit,
  output [15:0] Ouput
);

  wire Clock_out;
  wire [3:0] Register_q;

  Clock Clock (.out(Clock_out));
  Register #(.width(4)) Register (.D(Input_B), .en(Enable), .Q(Register_q), .clk(Clock_out), .clr(_1_Input_Bit));
  Shifter #(.width(16)) shifter_1 (.in(Input_A), .\dist (Register_q), .out(Ouput));

  // Notes on the sheet:
  //   16-Bit Left Shifter Circuit
  //   Shift A to left by B bits
endmodule

module _16_Bit_Right_Shfit_Circuit (
  input  [15:0] Input_A,
  input  [3:0] Input_B,
  input  Enable,
  input  _1_Input_Bit,
  output [15:0] Ouput
);

  wire Clock_out;
  wire [3:0] Register_q;

  Clock Clock (.out(Clock_out));
  Register #(.width(4)) Register (.D(Input_B), .en(Enable), .Q(Register_q), .clk(Clock_out), .clr(_1_Input_Bit));
  Shifter #(.width(16), .shift("lr")) shifter_1 (.in(Input_A), .\dist (Register_q), .out(Ouput));

  // Notes on the sheet:
  //   16-Bit Right Shifter Circuit
  //   Shift A to Right by B bits
endmodule

module Main_ALU_Circuit (
  output Overflow_bit
);


  // Notes on the sheet:
  //   Main ALU Circuit to Build
  //   Needs to use all the subcircuits you built
endmodule
