// Logisim project Updated ALU .circ as structural Verilog: 10 circuits, main circuit  Main ALU Circuit
module _16_Bit_AND (
  input  [15:0] Input_A,
  input  [15:0] Input_B,
  output [15:0] Output
);

  assign Output = Input_A & Input_B;  // AND_Gate AND, 16 bits wide

  // Notes on the sheet:
  //   16-Bit AND
endmodule

module _16_Bit_OR (
  input  [15:0] Input_A,
  input  [15:0] Input_B,
  output [15:0] Output
);

  assign Output = Input_A | Input_B;  // OR_Gate OR, 16 bits wide

  // Notes on the sheet:
  //   16-Bit OR
endmodule

module _16_Bit_XOR (
  input  [15:0] Input_A,
  input  [15:0] Input_B,
  output [15:0] out_3
);

  assign out_3 = Input_A ^ Input_B;  // XOR_Gate XOR, 16 bits wide

  // Notes on the sheet:
  //   16-bit XOR
endmodule

module _16_Bit_Inverter (
  input  [15:0] Input_A,
  output [15:0] Ouput
);

  assign Ouput = ~Input_A;  // NOT_Gate Not, 16 bits wide

  // Notes on the sheet:
  //   16-Bit Inverter
endmodule

module _16_Bit_Adder (
  input  Carry_in_Bit,
  input  [15:0] Input_A,
  input  [15:0] Input_B,
  input  Stand_for_S0_for_ALU,
  output Negative_flag,
  output [15:0] Ouput,
  output Zero_flag,
  output Carry_flag,
  output Overflow
);

  wire AND_2_out, AND_out, Not_2_out, Not_3_out, Not_out, XOR_out;

  Adder #(.width(16)) adder_1 (
    .a(Input_A), .b(Input_B), .out({Negative_flag, Ouput[14:0]}), .cin(Carry_in_Bit), .cout(Carry_flag));
  xor XOR (XOR_out, Input_B[15], Stand_for_S0_for_ALU);
  not Not (Not_out, Negative_flag);
  Comparator #(.width(16)) comparator_1 (
    .a({Negative_flag, Ouput[14:0]}), .b({16{1'b0}}), .eq(Zero_flag));  // open: gt, lt
  not Not_2 (Not_2_out, XOR_out);
  not Not_3 (Not_3_out, Input_A[15]);
  and AND (AND_out, XOR_out, Input_A[15]);
  and AND_2 (AND_2_out, Not_2_out, Not_3_out, Negative_flag);
  or OR (Overflow, AND_out, AND_2_out);

  assign Ouput[15] = Negative_flag;

  // Notes on the sheet:
  //   16-Bit Adder
  //   Please notice that you need to generate the four flag bits for the adder.
endmodule

module _16_Bit_Subtractor (
  input  Carry_in_Bit,
  input  [15:0] Input_A,
  input  [15:0] Input_B,
  input  Stand_for_S0_for_ALU,
  output Negative_flag,
  output [15:0] Ouput,
  output Zero_flag,
  output Carry_flag,
  output Overflow
);

  wire AND_2_out, AND_out, Not_2_out, Not_3_out, Not_out, XOR_out;

  Subtractor #(.width(16)) subtractor_1 (
    .a(Input_A), .b(Input_B), .out({Negative_flag, Ouput[14:0]}), .bin(Carry_in_Bit), .bout(Carry_flag));
  xor XOR (XOR_out, Input_B[15], Stand_for_S0_for_ALU);
  not Not (Not_out, Negative_flag);
  Comparator #(.width(16)) comparator_1 (
    .a({Negative_flag, Ouput[14:0]}), .b({16{1'b0}}), .eq(Zero_flag));  // open: gt, lt
  not Not_2 (Not_2_out, XOR_out);
  not Not_3 (Not_3_out, Input_A[15]);
  and AND (AND_out, XOR_out, Input_A[15]);
  and AND_2 (AND_2_out, Not_2_out, Not_3_out, Negative_flag);
  or OR (Overflow, AND_out, AND_2_out);

  assign Ouput[15] = Negative_flag;

  // Notes on the sheet:
  //   16-Bit Subtractor
  //   Please notice that you need to generate the four flag bits for the subtractor
endmodule

module _16_Bit_Left_Shifter_Circuit (
  input  [15:0] Input_A,
  input  [3:0] _4_Bit_Data,
  input  Enable_Bit,
  input  Clear_bit,
  output [15:0] Ouput
);

  wire Clock_out;
  wire [3:0] Register_q;

  Clock Clock (.out(Clock_out));
  Register #(.width(4)) Register (.D(_4_Bit_Data), .en(Enable_Bit), .Q(Register_q), .clk(Clock_out), .clr(Clear_bit));
  Shifter #(.width(16)) shifter_1 (.in(Input_A), .\dist (Register_q), .out(Ouput));

  // Notes on the sheet:
  //   16-Bit Left Shifter Circuit
  //   Shift A to left by B bits
endmodule

module _16_Bit_Right_Shfit_Circuit (
  input  [15:0] Input_A,
  input  [3:0] _4_Bit_Data,
  input  Enable_Bit,
  input  Clear_bit,
  output [15:0] Ouput
);

  wire Clock_out;
  wire [3:0] Register_q;

  Clock Clock (.out(Clock_out));
  Register #(.width(4)) Register (.D(_4_Bit_Data), .en(Enable_Bit), .Q(Register_q), .clk(Clock_out), .clr(Clear_bit));
  Shifter #(.width(16), .shift("lr")) shifter_1 (.in(Input_A), .\dist (Register_q), .out(Ouput));

  // Notes on the sheet:
  //   16-Bit Right Shifter Circuit
  //   Shift A to Right by B bits
endmodule

module _16_Bit_Adder_AI_Saturation (
  input  Carry_in,
  input  [15:0] Input_A,
  input  in_3,
  input  [15:0] Input_B,
  input  in_5,
  output Negative_flag,
  output [15:0] Saturation_Output,
  output [15:0] SUM,
  output Zero_flag,
  output Carry_flag,
  output Overflow_bit
);

  wire AND_2_out, AND_3_out, AND_4_out, AND_out, not_1_out, not_2_out, not_3_out, XOR_out;
  wire [15:0] multiplexer_1_out;

  Adder #(.width(16)) adder_1 (
    .a(Input_A), .b(Input_B), .out({Negative_flag, SUM[14:0]}), .cin(Carry_in), .cout(Carry_flag));
  xor XOR (XOR_out, Input_B[15], in_5);
  not not_1 (not_1_out, Negative_flag);
  Comparator #(.width(16)) comparator_1 (
    .a({Negative_flag, SUM[14:0]}), .b({16{1'b0}}), .eq(Zero_flag));  // open: gt, lt
  not not_2 (not_2_out, XOR_out);
  not not_3 (not_3_out, Input_A[15]);
  and AND (AND_out, XOR_out, not_1_out, Input_A[15]);
  and AND_2 (AND_2_out, not_2_out, not_3_out, Negative_flag);
  and AND_3 (AND_3_out, Negative_flag, Overflow_bit);
  or OR (Overflow_bit, AND_out, AND_2_out);
  Multiplexer #(.width(16)) multiplexer_1 (
    .in0(16'h8000), .in1(16'h7fff), .out(multiplexer_1_out), .sel(AND_3_out));  // open: en
  and AND_4 (AND_4_out, in_3, Overflow_bit);
  Multiplexer #(.width(16)) multiplexer_2 (
    .in0({Negative_flag, SUM[14:0]}), .in1(multiplexer_1_out), .out(Saturation_Output), .sel(AND_4_out));  // open: en

  assign SUM[15] = Negative_flag;

  // Notes on the sheet:
  //   16-Bit Adder AI Saturation
endmodule

module Main_ALU_Circuit (
  input  Carry_In,
  input  Borrow,
  input  [15:0] All_0,
  input  [15:0] Input_A,
  input  [15:0] Input_B,
  input  [2:0] in_6,
  output Negative_Flag,
  output Zero_Flag,
  output Carry_Flag,
  output Overflow_Flag,
  output [15:0] Result
);

  wire [2:2] n16_bit_subtractor_1_p5;
  wire [3:0] n16_bit_adder_1_negative_flag;
  wire [15:0] n16_bit_adder_1_ouput, n16_bit_and_1_output, n16_bit_inverter_1_ouput,
       n16_bit_left_shifter_circuit_1_p2, n16_bit_or_1_output, n16_bit_xor_1_out_3, undriven, undriven_2;

  _16_Bit_AND u_16_bit_and_1 (.Input_A(Input_A), .Input_B(Input_B), .Output(n16_bit_and_1_output));
  // _16_Bit_Left_Shifter_Circuit 16_bit_left_shifter_circuit_1: pin names not known; wires that end beside it: Input_A, n16_bit_left_shifter_circuit_1_p2
  _16_Bit_Adder u_16_bit_adder_1 (
    .Input_A(Input_A), .Input_B(Input_B), .Negative_flag(n16_bit_adder_1_negative_flag[0]),
    .Carry_in_Bit(Carry_In), .Ouput(n16_bit_adder_1_ouput), .Zero_flag(n16_bit_adder_1_negative_flag[1]),
    .Carry_flag(n16_bit_adder_1_negative_flag[2]), .Overflow(n16_bit_adder_1_negative_flag[3]),
    .Stand_for_S0_for_ALU(in_6[0]));
  // _16_Bit_Subtractor 16_bit_subtractor_1: pin names not known; wires that end beside it: Borrow, Input_A, Input_B, All_0, n16_bit_subtractor_1_p5[2]
  _16_Bit_OR u_16_bit_or_1 (.Input_A(Input_A), .Input_B(Input_B), .Output(n16_bit_or_1_output));
  _16_Bit_XOR u_16_bit_xor_1 (.Input_A(Input_A), .Input_B(Input_B), .out_3(n16_bit_xor_1_out_3));
  _16_Bit_Inverter u_16_bit_inverter_1 (.Input_A(Input_A), .Ouput(n16_bit_inverter_1_ouput));
  _16_Bit_Right_Shfit_Circuit u_16_bit_right_shfit_circuit_1 (.Input_A(Input_A));  // open: Ouput, _4_Bit_Data, Enable_Bit, Clear_bit
  Multiplexer #(.select(3), .width(16)) multiplexer_1 (
    .in0(n16_bit_adder_1_ouput), .in1(undriven_2), .in2(n16_bit_and_1_output), .in3(n16_bit_or_1_output),
    .in4(n16_bit_xor_1_out_3), .in5(n16_bit_inverter_1_ouput), .in6(undriven),
    .in7(n16_bit_left_shifter_circuit_1_p2), .out(Result), .sel(in_6));  // open: en
  Multiplexer #(.width(4)) multiplexer_2 (
    .in0(n16_bit_adder_1_negative_flag), .out({Overflow_Flag, Carry_Flag, Zero_Flag, Negative_Flag}),
    .sel(in_6[0]));  // open: in1, en

  // Notes on the sheet:
  //   Main ALU Circuit to Build
  //   Needs to use all the subcircuits you built
endmodule
